// Logisim project branch-comp.circ as structural Verilog: 1 circuit, main circuit branch_comp
module branch_comp (
  input  [31:0] BrData1,
  input  [31:0] BrData2,
  input  BrUn,
  output BrEq,
  output BrLt
);

  wire SignedCompEq, SignedCompLt, UnsignedCompEq, UnsignedCompLt;

  Comparator #(.mode("unsigned"), .width(32)) comparator_1 (
    .a(BrData1), .b(BrData2), .eq(UnsignedCompEq));  // open: gt, lt
  Comparator #(.width(32)) comparator_2 (.a(BrData1), .b(BrData2), .eq(SignedCompEq));  // open: gt, lt
  Comparator #(.mode("unsigned"), .width(32)) comparator_3 (
    .a(BrData1), .b(BrData2), .lt(UnsignedCompLt));  // open: gt, eq
  Comparator #(.width(32)) comparator_4 (.a(BrData1), .b(BrData2), .lt(SignedCompLt));  // open: gt, eq
  Multiplexer multiplexer_1 (.in0(SignedCompEq), .in1(UnsignedCompEq), .out(BrEq), .sel(BrUn));
  Multiplexer multiplexer_2 (.in0(SignedCompLt), .in1(UnsignedCompLt), .out(BrLt), .sel(BrUn));

  // Notes on the sheet:
  //   INPUTS to your circuit
  //   DON'T CHANGE THE LOCATIONS OF THE INPUTS AND OUTPUTS!
  //   OUTPUT from your circuit
endmodule
