// Logisim project control-logic.circ as structural Verilog: 1 circuit, main circuit control_logic
module control_logic (
  input  [31:0] Instruction,
  input  BrEq,
  input  BrLt,
  output PCSel,
  output RegWEn,
  output [2:0] ImmSel,
  output BrUn,
  output ASel,
  output BSel,
  output [3:0] ALUSel,
  output MemWEn,
  output [1:0] WBSel
);

  wire and_36_out, and_37_out, and_38_out, and_39_out, and_40_out, and_41_out, is_add, is_addi, is_Ai,
       is_and, is_andi, is_auipc, is_B, is_beq, is_bge, is_bgeu, is_blt, is_bltu, is_bne, is_jal, is_jalr,
       is_Ji, is_lb, is_lh, is_Li, is_lui, is_lw, is_mul, is_mulh, is_mulhu, is_or, is_ori, is_R, is_S,
       is_sb, is_sh, is_sll, is_slli, is_slt, is_slti, is_sra, is_srai, is_srl, is_srli, is_sub, is_sw,
       is_UA, is_UL, is_xor, is_xori, not_1_out, not_2_out, not_3_out, or_1_out, or_2_out, seven_0, seven_1,
       seven_20, three_0, three_1, three_2, three_3, three_4, three_5, three_6, three_7;
  wire [5:0] ROM_INPUT;
  wire [15:14] rom_1_data;

  Comparator #(.mode("unsigned"), .width(7)) comparator_1 (
    .a(7'b0100011), .b(Instruction[6:0]), .eq(is_S));  // open: gt, lt
  Comparator #(.mode("unsigned"), .width(7)) comparator_2 (
    .a(7'b1100011), .b(Instruction[6:0]), .eq(is_B));  // open: gt, lt
  Comparator #(.mode("unsigned"), .width(7)) comparator_3 (
    .a(7'b0010111), .b(Instruction[6:0]), .eq(is_UA));  // open: gt, lt
  Comparator #(.mode("unsigned"), .width(7)) comparator_4 (
    .a(7'b0110111), .b(Instruction[6:0]), .eq(is_UL));  // open: gt, lt
  Comparator #(.mode("unsigned"), .width(7)) comparator_5 (
    .a(7'b1101111), .b(Instruction[6:0]), .eq(is_jal));  // open: gt, lt
  Comparator #(.mode("unsigned"), .width(7)) comparator_6 (
    .a(7'b1100111), .b(Instruction[6:0]), .eq(is_Ji));  // open: gt, lt
  Comparator #(.width(7)) comparator_7 (.a({7{1'b0}}), .b(Instruction[31:25]), .eq(seven_0));  // open: gt, lt
  Comparator #(.mode("unsigned"), .width(7)) comparator_8 (
    .a(7'b0110011), .b(Instruction[6:0]), .eq(is_R));  // open: gt, lt
  Comparator #(.mode("unsigned"), .width(7)) comparator_9 (
    .a(7'b0000011), .b(Instruction[6:0]), .eq(is_Li));  // open: gt, lt
  Comparator #(.mode("unsigned"), .width(7)) comparator_10 (
    .a(7'b0010011), .b(Instruction[6:0]), .eq(is_Ai));  // open: gt, lt
  Comparator #(.width(3)) comparator_11 (.a(3'b000), .b(Instruction[14:12]), .eq(three_0));  // open: gt, lt
  Comparator #(.width(3)) comparator_12 (.a(3'b001), .b(Instruction[14:12]), .eq(three_1));  // open: gt, lt
  Comparator #(.width(3)) comparator_13 (.a(3'b010), .b(Instruction[14:12]), .eq(three_2));  // open: gt, lt
  Comparator #(.width(3)) comparator_14 (.a(3'b011), .b(Instruction[14:12]), .eq(three_3));  // open: gt, lt
  Comparator #(.width(3)) comparator_15 (.a(3'b100), .b(Instruction[14:12]), .eq(three_4));  // open: gt, lt
  Comparator #(.width(3)) comparator_16 (.a(3'b101), .b(Instruction[14:12]), .eq(three_5));  // open: gt, lt
  Comparator #(.width(3)) comparator_17 (.a(3'b110), .b(Instruction[14:12]), .eq(three_6));  // open: gt, lt
  Comparator #(.width(3)) comparator_18 (.a(3'b111), .b(Instruction[14:12]), .eq(three_7));  // open: gt, lt
  Comparator #(.width(7)) comparator_19 (.a(7'b0000001), .b(Instruction[31:25]), .eq(seven_1));  // open: gt, lt
  Comparator #(.width(7)) comparator_20 (.a(7'b0100000), .b(Instruction[31:25]), .eq(seven_20));  // open: gt, lt
  ROM #(.addrWidth(6), .dataWidth(16)) rom_1 (
    .addr(ROM_INPUT), .data({rom_1_data, WBSel, MemWEn, ALUSel, BSel, ASel, BrUn, ImmSel, RegWEn}));
  and and_1 (is_ori, is_Ai, three_6);
  and and_2 (is_andi, is_Ai, three_7);
  and and_3 (is_sh, is_S, three_1);
  and and_4 (is_sw, is_S, three_2);
  and and_5 (is_beq, is_B, three_0);
  and and_6 (is_bne, is_B, three_1);
  and and_7 (is_blt, is_B, three_4);
  and and_8 (is_bge, is_B, three_5);
  and and_9 (is_bltu, is_B, three_6);
  and and_10 (is_bgeu, is_B, three_7);
  and and_11 (is_auipc, is_UA, 1'b1);
  and and_12 (is_lui, is_UL, 1'b1);
  and and_13 (is_jalr, is_Ji, three_0);
  and and_14 (is_srai, is_Ai, seven_20, three_5);
  and and_15 (is_sb, is_S, three_0);
  and and_16 (is_add, is_R, three_0, seven_0);
  and and_17 (is_mul, is_R, three_0, seven_1);
  and and_18 (is_sub, is_R, three_0, seven_20);
  and and_19 (is_sll, is_R, three_1, seven_0);
  and and_20 (is_mulh, is_R, three_1, seven_1);
  and and_21 (is_mulhu, is_R, three_3, seven_1);
  and and_22 (is_slt, is_R, three_2, seven_0);
  and and_23 (is_xor, is_R, three_4, seven_0);
  and and_24 (is_srl, is_R, three_5, seven_0);
  and and_25 (is_sra, is_R, three_5, seven_20);
  and and_26 (is_or, is_R, three_6, seven_0);
  and and_27 (is_and, is_R, three_7, seven_0);
  and and_28 (is_lb, is_Li, three_0);
  and and_29 (is_lh, is_Li, three_1);
  and and_30 (is_lw, is_Li, three_2);
  and and_31 (is_addi, is_Ai, three_0);
  and and_32 (is_slli, is_Ai, three_1, seven_0);
  and and_33 (is_slti, is_Ai, three_2);
  and and_34 (is_xori, is_Ai, three_4);
  and and_35 (is_srli, is_Ai, seven_0, three_5);
  not not_1 (not_1_out, BrEq);
  not not_2 (not_2_out, BrLt);
  not not_3 (not_3_out, BrLt);
  and and_36 (and_36_out, is_beq, BrEq);
  and and_37 (and_37_out, is_bne, not_1_out);
  and and_38 (and_38_out, is_bltu, BrLt);
  and and_39 (and_39_out, is_blt, BrLt);
  and and_40 (and_40_out, is_bgeu, not_2_out);
  and and_41 (and_41_out, is_bge, not_3_out);
  or or_1 (or_1_out, and_36_out, and_37_out, and_38_out, and_39_out, and_40_out, and_41_out);
  or or_2 (or_2_out, is_jal, is_jalr);
  or or_3 (PCSel, or_1_out, or_2_out);
  Priority_Encoder #(.select_enc(6)) priority_encoder_1 (
    .in0(is_add), .in1(is_mul), .in2(is_sub), .in3(is_sll), .in4(is_mulh), .in5(is_mulhu), .in6(is_slt),
    .in7(is_xor), .in8(is_srl), .in9(is_sra), .in10(is_or), .in11(is_and), .in12(is_lb), .in13(is_lh),
    .in14(is_lw), .in15(is_addi), .in16(is_slli), .in17(is_slti), .in18(is_xori), .in19(is_srli),
    .in20(is_srai), .in21(is_ori), .in22(is_andi), .in23(is_sb), .in24(is_sh), .in25(is_sw), .in26(is_beq),
    .in27(is_bne), .in28(is_blt), .in29(is_bge), .in30(is_bltu), .in31(is_bgeu), .in32(is_auipc),
    .in33(is_lui), .in34(is_jal), .in35(is_jalr), .out(ROM_INPUT));  // open: in36, in37, in38, in39, in40, in41, in42, in43, in44, in45, in46, in47, in48, in49, in50, in51, in52, in53, in54, in55, in56, in57, in58, in59, in60, in61, in62, in63, gs, en_out, en_in

  // Other names for the same wires on the sheet: funct3[2:0] = Instruction[14:12]; funct7[6:0] = Instruction[31:25]

  // Notes on the sheet:
  //   INPUTS to your circuit
  //   Connect ROM Input here ->
  //   contents of rom_1 (hex, n*v repeats v):
  //   1001 1401 1601 1081 1481 1581 1101 1201 1281 1681 1301 1381 41 41 41 1041 10c1 1141 1241 12c1 16c1
  //   1341 13c1 842 842 842 4*64 74 74 1067 17c7 2069 2041
  //   ROM FOR CONTROL LOGIC
  //   DON'T CHANGE THE LOCATIONS OF THE INPUTS AND OUTPUTS!
  //   This is only if you choose to do the ROM option
  //   CONNECT
  //   WIRE
  //   TO
  //   USE
  //   ROM
  //   OUTPUT from your circuit
  //   Reminder: If using ROM, use combinational logic for PCSel
endmodule
