// Logisim project cpu.circ as structural Verilog: 1 circuit, main circuit cpu
module cpu (
  input  clk,
  input  [31:0] Instruction,
  input  [31:0] MemReadData,
  output [31:0] MemAddress,
  output [31:0] ProgramCounter,
  output [31:0] ra,
  output [31:0] sp,
  output [31:0] t0,
  output [31:0] t1,
  output [31:0] t2,
  output [31:0] s0,
  output [31:0] s1,
  output [31:0] a0,
  output [3:0] MemWriteMask,
  output [31:0] MemWriteData
);

  wire ASel, BrEq, BrLt, BrUn, BSel, MemWEn, PCSel, RegWEn;
  wire [1:0] WBSel;
  wire [2:0] ImmSel;
  wire [3:0] ALUSel;
  wire [4:0] inst_11_to_7, inst_19_to_15, inst_24_to_20;
  wire [31:0] DataToReg, ImmGen_out, Instruction2, multiplexer_1_out, multiplexer_2_out, multiplexer_3_out,
       multiplexer_4_out, PC2_plus_4, PC_plus_4, ProgramCounter2, RegReadData1, RegReadData2, WriteData;

  Register #(.width(32)) Inst (
    .D(multiplexer_2_out), .clk(clk),
    .Q({Instruction2[31:25], inst_24_to_20, inst_19_to_15, Instruction2[14:12], inst_11_to_7, Instruction2[6:0]}));  // open: en, clr
  Register #(.width(32)) PC (.D(multiplexer_1_out), .clk(clk), .Q(ProgramCounter));  // open: en, clr
  Multiplexer #(.width(32)) multiplexer_1 (.in0(PC_plus_4), .in1(MemAddress), .out(multiplexer_1_out), .sel(PCSel));
  Multiplexer #(.width(32)) multiplexer_2 (.in0(Instruction), .in1(32'h13), .out(multiplexer_2_out), .sel(PCSel));
  Adder #(.width(32)) adder_1 (.a(ProgramCounter), .b(32'h4), .out(PC_plus_4));  // open: cin, cout
  Register #(.width(32)) register_1 (.D(ProgramCounter), .clk(clk), .Q(ProgramCounter2));  // open: en, clr
  regfile regfile_1 (
    .ReadIndex1(inst_19_to_15), .ReadIndex2(inst_24_to_20), .WriteIndex(inst_11_to_7), .WriteData(WriteData),
    .RegWEn(RegWEn), .clk(clk), .ra(ra), .sp(sp), .t0(t0), .t1(t1), .t2(t2), .s0(s0), .s1(s1), .a0(a0),
    .ReadData1(RegReadData1), .ReadData2(RegReadData2));
  control_logic control_logic_1 (
    .Instruction({Instruction2[31:25], inst_24_to_20, inst_19_to_15, Instruction2[14:12], inst_11_to_7, Instruction2[6:0]}),
    .BrEq(BrEq), .BrLt(BrLt), .PCSel(PCSel), .RegWEn(RegWEn), .ImmSel(ImmSel), .BrUn(BrUn), .ASel(ASel),
    .BSel(BSel), .ALUSel(ALUSel), .MemWEn(MemWEn), .WBSel(WBSel));
  imm_gen imm_gen_1 (
    .Instruction({Instruction2[31:25], inst_24_to_20, inst_19_to_15, Instruction2[14:12], inst_11_to_7, Instruction2[6:0]}),
    .ImmSel(ImmSel), .Immediate(ImmGen_out));
  branch_comp branch_comp_1 (.BrData1(RegReadData1), .BrData2(RegReadData2), .BrUn(BrUn), .BrEq(BrEq), .BrLt(BrLt));
  Adder #(.width(32)) adder_2 (.a(ProgramCounter2), .b(32'h4), .out(PC2_plus_4));  // open: cin, cout
  Multiplexer #(.width(32)) multiplexer_3 (
    .in0(RegReadData1), .in1(ProgramCounter2), .out(multiplexer_3_out), .sel(ASel));
  Multiplexer #(.width(32)) multiplexer_4 (.in0(RegReadData2), .in1(ImmGen_out), .out(multiplexer_4_out), .sel(BSel));
  alu alu_1 (.A(multiplexer_3_out), .B(multiplexer_4_out), .ALUSel(ALUSel), .ALUResult(MemAddress));
  partial_store partial_store_1 (
    .Instruction({Instruction2[31:25], inst_24_to_20, inst_19_to_15, Instruction2[14:12], inst_11_to_7, Instruction2[6:0]}),
    .MemAddress(MemAddress), .DataFromReg(RegReadData2), .MemWEn(MemWEn), .MemWriteMask(MemWriteMask),
    .DataToMem(MemWriteData));
  partial_load partial_load_1 (
    .Instruction({Instruction2[31:25], inst_24_to_20, inst_19_to_15, Instruction2[14:12], inst_11_to_7, Instruction2[6:0]}),
    .MemAddress(MemAddress), .DataFromMem(MemReadData), .DataToReg(DataToReg));
  Multiplexer #(.select(2), .width(32)) multiplexer_5 (
    .in0(DataToReg), .in1(MemAddress), .in2(PC2_plus_4), .out(WriteData), .sel(WBSel));  // open: in3

  // Other names for the same wires on the sheet: ALU_out[31:0] = MemAddress;
  //   Instruction2 (some bits) = {inst_24_to_20, inst_19_to_15, inst_11_to_7}

  // Notes on the sheet:
  //   To IMEM
  //   IMEM (do **NOT** move this)
  //   From IMEM
  //   Inputs/Outputs for testing. Do **NOT** move these.
  //   It is OK to move the PC, RegFile, ALU, MEM, Branch Comp, Imm Gen, Partial Load, Partial Store and Control Logic to wherever is most convenient for you when constructing your CPU, and to delete this text
  //   To DMEM
  //   DMEM (do **NOT** move this)
  //   From DMEM
endmodule
