// Logisim project partial-load.circ as structural Verilog: 1 circuit, main circuit partial_load
module partial_load (
  input  [31:0] Instruction,
  input  [31:0] MemAddress,
  input  [31:0] DataFromMem,
  output [31:0] DataToReg
);

  wire [1:0] index;
  wire [4:0] bit_extender_1_out, multiplier_1_out;
  wire [7:0] bit_extender_2_out;
  wire [15:0] bit_extender_3_out;
  wire [31:0] load, load_byte, load_half_word;

  assign bit_extender_1_out = {{3{1'b0}}, index};  // Bit_Extender bit_extender_1
  Multiplier #(.width(5)) multiplier_1 (
    .a(bit_extender_1_out), .b(5'b01000), .out(multiplier_1_out));  // open: cin, cout
  Bit_Extender #(.in_width(32), .out_width(8)) bit_extender_2 (.in(load), .out(bit_extender_2_out));
  Bit_Extender #(.in_width(32)) bit_extender_3 (.in(load), .out(bit_extender_3_out));
  Bit_Extender #(.in_width(32), .out_width(2)) bit_extender_4 (.in(MemAddress), .out(index));
  Shifter #(.shift("ar"), .width(32)) shifter_1 (.in(DataFromMem), .\dist (multiplier_1_out), .out(load));
  assign load_byte = {{24{bit_extender_2_out[7]}}, bit_extender_2_out};  // Bit_Extender bit_extender_5
  assign load_half_word = {{16{bit_extender_3_out[15]}}, bit_extender_3_out};  // Bit_Extender bit_extender_6
  Multiplexer #(.select(3), .width(32)) multiplexer_1 (
    .in0(load_byte), .in1(load_half_word), .in2(load), .out(DataToReg), .sel(Instruction[14:12]));  // open: in3, in4, in5, in6, in7

  // Other names for the same wires on the sheet: funct3[2:0] = Instruction[14:12]; load_word[31:0] = load

  // Notes on the sheet:
  //   INPUTS to your circuit
  //   DON'T CHANGE THE LOCATIONS OF THE INPUTS AND OUTPUTS!
  //   OUTPUT from your circuit
endmodule
