// Logisim project partial-store.circ as structural Verilog: 1 circuit, main circuit partial_store
module partial_store (
  input  [31:0] Instruction,
  input  [31:0] MemAddress,
  input  [31:0] DataFromReg,
  input  MemWEn,
  output [3:0] MemWriteMask,
  output [31:0] DataToMem
);

  wire [1:0] index, store_type_shift;
  wire [3:0] bit_extender_3_out, MemWriteMask_Temp, shifter_1_out, shifter_2_out, shifter_3_out;
  wire [4:0] bit_extender_1_out, bit_extender_4_out, multiplier_1_out, multiplier_2_out;
  wire [31:0] shifter_6_out;

  Multiplexer #(.select(3), .width(2)) multiplexer_1 (
    .in0(2'b11), .in1(2'b10), .in2(2'b00), .out(store_type_shift), .sel(Instruction[14:12]));  // open: in3, in4, in5, in6, in7
  assign bit_extender_1_out = {{3{1'b0}}, index};  // Bit_Extender bit_extender_1
  Shifter #(.shift("lr"), .width(4)) shifter_1 (.in(4'b1111), .\dist (index), .out(shifter_1_out));
  Bit_Extender #(.in_width(32), .out_width(2)) bit_extender_2 (.in(MemAddress), .out(index));
  Multiplier #(.width(5)) multiplier_1 (
    .a(bit_extender_1_out), .b(5'b01000), .out(multiplier_1_out));  // open: cin, cout
  Shifter #(.width(4)) shifter_2 (.in(shifter_1_out), .\dist (store_type_shift), .out(shifter_2_out));
  Shifter #(.shift("lr"), .width(4)) shifter_3 (.in(shifter_2_out), .\dist (store_type_shift), .out(shifter_3_out));
  Shifter #(.width(32)) shifter_4 (.in(DataFromReg), .\dist (multiplier_1_out), .out(DataToMem));
  Shifter #(.width(4)) shifter_5 (.in(shifter_3_out), .\dist (index), .out(MemWriteMask_Temp));
  assign bit_extender_3_out = {{3{MemWEn}}, MemWEn};  // Bit_Extender bit_extender_3
  assign MemWriteMask = MemWriteMask_Temp & bit_extender_3_out;  // AND_Gate and_1, 4 bits wide
  assign bit_extender_4_out = {{3{1'b0}}, index};  // Bit_Extender bit_extender_4
  Multiplier #(.width(5)) multiplier_2 (
    .a(bit_extender_4_out), .b(5'b01000), .out(multiplier_2_out));  // open: cin, cout
  Shifter #(.shift("lr"), .width(32)) shifter_6 (.in(DataFromReg), .\dist (multiplier_2_out), .out(shifter_6_out));
  Shifter #(.width(32)) shifter_7 (.in(shifter_6_out), .\dist (multiplier_2_out));  // open: out

  // Other names for the same wires on the sheet: funct3[2:0] = Instruction[14:12]

  // Notes on the sheet:
  //   INPUTS to your circuit
  //   DON'T CHANGE THE LOCATIONS OF THE INPUTS AND OUTPUTS!
  //   OUTPUT from your circuit
endmodule
