// Logisim project regfile.circ as structural Verilog: 1 circuit, main circuit regfile
module regfile (
  input  [4:0] ReadIndex1,
  input  [4:0] ReadIndex2,
  input  [4:0] WriteIndex,
  input  [31:0] WriteData,
  input  RegWEn,
  input  clk,
  output [31:0] ra,
  output [31:0] sp,
  output [31:0] t0,
  output [31:0] t1,
  output [31:0] t2,
  output [31:0] s0,
  output [31:0] s1,
  output [31:0] a0,
  output [31:0] ReadData1,
  output [31:0] ReadData2
);

  wire a0_WEn, a1_WEn, a2_WEn, a3_WEn, a4_WEn, a5_WEn, a6_WEn, a7_WEn, gp_WEn, ra_WEn, s0_WEn, s1_WEn,
       s2_WEn, s3_WEn, s4_WEn, s5_WEn, s6_WEn, s7_WEn, s8_WEn, s9_WEn, s10_WEn, s11_WEn, sp_WEn, t0_WEn,
       t1_WEn, t2_WEn, t3_WEn, t4_WEn, t5_WEn, t6_WEn, tp_WEn, zero_WEn;
  wire [31:0] a0_in, a1, a1_in, a2, a2_in, a3, a3_in, a4, a4_in, a5, a5_in, a6, a6_in, a7, a7_in, gp, gp_in,
       ra_in, s0_in, s1_in, s2, s2_in, s3, s3_in, s4, s4_in, s5, s5_in, s6, s6_in, s7, s7_in, s8, s8_in, s9,
       s9_in, s10, s10_in, s11, s11_in, sp_in, t0_in, t1_in, t2_in, t3, t3_in, t4, t4_in, t5, t5_in, t6,
       t6_in, tp, tp_in, zero, zero_in;

  Register #(.width(32)) register_1 (.D({32{1'b0}}), .en(zero_WEn), .clk(clk), .Q(zero));  // open: clr
  Register #(.width(32)) register_2 (.D(ra_in), .en(ra_WEn), .clk(clk), .Q(ra));  // open: clr
  Register #(.width(32)) register_3 (.D(sp_in), .en(sp_WEn), .clk(clk), .Q(sp));  // open: clr
  Register #(.width(32)) register_4 (.D(gp_in), .en(gp_WEn), .clk(clk), .Q(gp));  // open: clr
  Register #(.width(32)) register_5 (.D(tp_in), .en(tp_WEn), .clk(clk), .Q(tp));  // open: clr
  Register #(.width(32)) register_6 (.D(t0_in), .en(t0_WEn), .clk(clk), .Q(t0));  // open: clr
  Register #(.width(32)) register_7 (.D(t1_in), .en(t1_WEn), .clk(clk), .Q(t1));  // open: clr
  Register #(.width(32)) register_8 (.D(t3_in), .en(t3_WEn), .clk(clk), .Q(t3));  // open: clr
  Register #(.width(32)) register_9 (.D(t2_in), .en(t2_WEn), .clk(clk), .Q(t2));  // open: clr
  Register #(.width(32)) register_10 (.D(s0_in), .en(s0_WEn), .clk(clk), .Q(s0));  // open: clr
  Register #(.width(32)) register_11 (.D(s1_in), .en(s1_WEn), .clk(clk), .Q(s1));  // open: clr
  Register #(.width(32)) register_12 (.D(a0_in), .en(a0_WEn), .clk(clk), .Q(a0));  // open: clr
  Register #(.width(32)) register_13 (.D(a1_in), .en(a1_WEn), .clk(clk), .Q(a1));  // open: clr
  Register #(.width(32)) register_14 (.D(a2_in), .en(a2_WEn), .clk(clk), .Q(a2));  // open: clr
  Register #(.width(32)) register_15 (.D(a3_in), .en(a3_WEn), .clk(clk), .Q(a3));  // open: clr
  Register #(.width(32)) register_16 (.D(t4_in), .en(t4_WEn), .clk(clk), .Q(t4));  // open: clr
  Register #(.width(32)) register_17 (.D(a4_in), .en(a4_WEn), .clk(clk), .Q(a4));  // open: clr
  Register #(.width(32)) register_18 (.D(a5_in), .en(a5_WEn), .clk(clk), .Q(a5));  // open: clr
  Register #(.width(32)) register_19 (.D(a6_in), .en(a6_WEn), .clk(clk), .Q(a6));  // open: clr
  Register #(.width(32)) register_20 (.D(a7_in), .en(a7_WEn), .clk(clk), .Q(a7));  // open: clr
  Register #(.width(32)) register_21 (.D(s2_in), .en(s2_WEn), .clk(clk), .Q(s2));  // open: clr
  Register #(.width(32)) register_22 (.D(s3_in), .en(s3_WEn), .clk(clk), .Q(s3));  // open: clr
  Register #(.width(32)) register_23 (.D(s4_in), .en(s4_WEn), .clk(clk), .Q(s4));  // open: clr
  Register #(.width(32)) register_24 (.D(t5_in), .en(t5_WEn), .clk(clk), .Q(t5));  // open: clr
  Register #(.width(32)) register_25 (.D(s5_in), .en(s5_WEn), .clk(clk), .Q(s5));  // open: clr
  Register #(.width(32)) register_26 (.D(s6_in), .en(s6_WEn), .clk(clk), .Q(s6));  // open: clr
  Register #(.width(32)) register_27 (.D(s7_in), .en(s7_WEn), .clk(clk), .Q(s7));  // open: clr
  Register #(.width(32)) register_28 (.D(s8_in), .en(s8_WEn), .clk(clk), .Q(s8));  // open: clr
  Register #(.width(32)) register_29 (.D(s9_in), .en(s9_WEn), .clk(clk), .Q(s9));  // open: clr
  Register #(.width(32)) register_30 (.D(s10_in), .en(s10_WEn), .clk(clk), .Q(s10));  // open: clr
  Register #(.width(32)) register_31 (.D(s11_in), .en(s11_WEn), .clk(clk), .Q(s11));  // open: clr
  Register #(.width(32)) register_32 (.D(t6_in), .en(t6_WEn), .clk(clk), .Q(t6));  // open: clr
  Multiplexer #(.select(5), .width(32)) multiplexer_1 (
    .in0(zero), .in1(ra), .in2(sp), .in3(gp), .in4(tp), .in5(t0), .in6(t1), .in7(t2), .in8(s0), .in9(s1),
    .in10(a0), .in11(a1), .in12(a2), .in13(a3), .in14(a4), .in15(a5), .in16(a6), .in17(a7), .in18(s2),
    .in19(s3), .in20(s4), .in21(s5), .in22(s6), .in23(s7), .in24(s8), .in25(s9), .in26(s10), .in27(s11),
    .in28(t3), .in29(t4), .in30(t5), .in31(t6), .out(ReadData1), .sel(ReadIndex1));
  Multiplexer #(.select(5), .width(32)) multiplexer_2 (
    .in0(zero), .in1(ra), .in2(sp), .in3(gp), .in4(tp), .in5(t0), .in6(t1), .in7(t2), .in8(s0), .in9(s1),
    .in10(a0), .in11(a1), .in12(a2), .in13(a3), .in14(a4), .in15(a5), .in16(a6), .in17(a7), .in18(s2),
    .in19(s3), .in20(s4), .in21(s5), .in22(s6), .in23(s7), .in24(s8), .in25(s9), .in26(s10), .in27(s11),
    .in28(t3), .in29(t4), .in30(t5), .in31(t6), .out(ReadData2), .sel(ReadIndex2));
  Demultiplexer #(.select(5), .width(32)) demultiplexer_1 (
    .out0(zero_in), .out1(ra_in), .out2(sp_in), .out3(gp_in), .out4(tp_in), .out5(t0_in), .out6(t1_in),
    .out7(t2_in), .out8(s0_in), .out9(s1_in), .out10(a0_in), .out11(a1_in), .out12(a2_in), .out13(a3_in),
    .out14(a4_in), .out15(a5_in), .out16(a6_in), .out17(a7_in), .out18(s2_in), .out19(s3_in), .out20(s4_in),
    .out21(s5_in), .out22(s6_in), .out23(s7_in), .out24(s8_in), .out25(s9_in), .out26(s10_in),
    .out27(s11_in), .out28(t3_in), .out29(t4_in), .out30(t5_in), .out31(t6_in), .in(WriteData),
    .sel(WriteIndex));
  Demultiplexer #(.select(5)) demultiplexer_2 (
    .out0(zero_WEn), .out1(ra_WEn), .out2(sp_WEn), .out3(gp_WEn), .out4(tp_WEn), .out5(t0_WEn),
    .out6(t1_WEn), .out7(t2_WEn), .out8(s0_WEn), .out9(s1_WEn), .out10(a0_WEn), .out11(a1_WEn),
    .out12(a2_WEn), .out13(a3_WEn), .out14(a4_WEn), .out15(a5_WEn), .out16(a6_WEn), .out17(a7_WEn),
    .out18(s2_WEn), .out19(s3_WEn), .out20(s4_WEn), .out21(s5_WEn), .out22(s6_WEn), .out23(s7_WEn),
    .out24(s8_WEn), .out25(s9_WEn), .out26(s10_WEn), .out27(s11_WEn), .out28(t3_WEn), .out29(t4_WEn),
    .out30(t5_WEn), .out31(t6_WEn), .in(RegWEn), .sel(WriteIndex));

  // Notes on the sheet:
  //   INPUTS to your circuit
  //   DON'T CHANGE THE LOCATIONS OF THE INPUTS AND OUTPUTS!
  //   These are DEBUG/TEST outputs from your circuit.
  //   OUTPUTS from your circuit
endmodule
